# Fritzing sketch single_seven_segment (saved by Fritzing 0.9.0b)
breadboards: 1

parts:
  Part1 = Arduino Uno (Rev3)
  7_Segment1 = 7 Segment Display
  R1 = Resistor [tolerance=±5% resistance=220 package=THT]

nets:
  N1: Part1.D8, 7_Segment1.Segment_F
  N2: Part1.D9_PWM, 7_Segment1.Segment_G
  N3: Part1.D10_PWM/SS, 7_Segment1.Segment_DP
  N4: Part1.D11_PWM/MOSI, 7_Segment1.Segment_C
  N5: Part1.D12/MISO, 7_Segment1.Segment_B
  N6: Part1.D13/SCK, 7_Segment1.Segment_A
  N7: Part1.D6_PWM, 7_Segment1.Segment_D
  N8: Part1.D7, 7_Segment1.Segment_E
  N9: Part1.GND, R1.Pin_1
  N10: 7_Segment1.common_anode, R1.Pin_0
